// Logisim project 1+exponent.circ as structural Verilog: 1 circuit, main circuit 1+exponent
module _1_exponent (
  input  [8:0] exponent,
  input  control_bit,
  output [8:0] exponent_controlbit,
  output overflow,
  output INF
);

  wire comparator_1_eq, comparator_2_eq;

  Adder #(.width(9)) adder_1 (
    .a(exponent), .b({{8{1'b0}}, control_bit}), .out(exponent_controlbit), .cin(1'b0), .cout(overflow));
  Comparator #(.width(10)) comparator_1 (
    .a(10'h1ff), .b({1'b0, exponent_controlbit}), .eq(comparator_1_eq));  // open: gt, lt
  or or_1 (INF, comparator_2_eq, comparator_1_eq);
  Comparator #(.width(10)) comparator_2 (.a({1'b0, exponent}), .b(10'h1ff), .eq(comparator_2_eq));  // open: gt, lt
endmodule
