// Logisim project 2s_Complementer.circ as structural Verilog: 1 circuit, main circuit 2s_complement
module _2s_complement (
  input  [31:0] input_32_bit,
  output [31:0] output32
);

  wire [31:0] not_1_out;

  not not_1 (not_1_out[0], input_32_bit[0]);
  not not_2 (not_1_out[2], input_32_bit[2]);
  not not_3 (not_1_out[4], input_32_bit[4]);
  not not_4 (not_1_out[6], input_32_bit[6]);
  not not_5 (not_1_out[8], input_32_bit[8]);
  not not_6 (not_1_out[10], input_32_bit[10]);
  not not_7 (not_1_out[12], input_32_bit[12]);
  not not_8 (not_1_out[14], input_32_bit[14]);
  not not_9 (not_1_out[16], input_32_bit[16]);
  not not_10 (not_1_out[18], input_32_bit[18]);
  not not_11 (not_1_out[20], input_32_bit[20]);
  not not_12 (not_1_out[22], input_32_bit[22]);
  not not_13 (not_1_out[24], input_32_bit[24]);
  not not_14 (not_1_out[26], input_32_bit[26]);
  not not_15 (not_1_out[28], input_32_bit[28]);
  not not_16 (not_1_out[30], input_32_bit[30]);
  not not_17 (not_1_out[1], input_32_bit[1]);
  not not_18 (not_1_out[3], input_32_bit[3]);
  not not_19 (not_1_out[5], input_32_bit[5]);
  not not_20 (not_1_out[7], input_32_bit[7]);
  not not_21 (not_1_out[9], input_32_bit[9]);
  not not_22 (not_1_out[11], input_32_bit[11]);
  not not_23 (not_1_out[13], input_32_bit[13]);
  not not_24 (not_1_out[15], input_32_bit[15]);
  not not_25 (not_1_out[17], input_32_bit[17]);
  not not_26 (not_1_out[19], input_32_bit[19]);
  not not_27 (not_1_out[21], input_32_bit[21]);
  not not_28 (not_1_out[23], input_32_bit[23]);
  not not_29 (not_1_out[25], input_32_bit[25]);
  not not_30 (not_1_out[27], input_32_bit[27]);
  not not_31 (not_1_out[29], input_32_bit[29]);
  not not_32 (not_1_out[31], input_32_bit[31]);
  Adder #(.width(32)) adder_1 (.a(not_1_out), .b({32{1'b0}}), .out(output32), .cin(1'b1));  // open: cout
endmodule
