// Logisim project abs32.circ as structural Verilog: 1 circuit, main circuit absolute_val_significand
// abs
module absolute_val_significand (
  input  [31:0] input32,
  input  SignbitIn,
  output [31:0] output32
);

  wire adder_1_cout;
  wire [31:0] xor_1_out;

  assign xor_1_out = input32 ^ {32{SignbitIn}};  // XOR_Gate xor_1, 32 bits wide
  Adder #(.width(32)) adder_1 (.a(xor_1_out), .b({32{1'b0}}), .out(output32), .cin(SignbitIn), .cout(adder_1_cout));
endmodule
