// Logisim project adder_sub_32bit.circ as structural Verilog: 1 circuit, main circuit adder_sub
// adder/sub
module adder_sub (
  input  [31:0] inputB32,
  input  control,
  input  [31:0] inputA32,
  output sign_bit,
  output [31:0] output32,
  output cout
);

  wire adder_1_cout, comparator_1_gt, not_1_out;
  wire [31:0] multiplexer_1_out, n2s_complement_1_output32;

  not not_1 (not_1_out, control);
  Multiplexer #(.width(32), .enable("false")) multiplexer_1 (
    .in0(inputB32), .in1(n2s_complement_1_output32), .out(multiplexer_1_out), .sel(not_1_out));
  _2s_complement u_2s_complement_1 (.input_32_bit(inputB32), .output32(n2s_complement_1_output32));
  Adder #(.width(32)) adder_1 (.a(multiplexer_1_out), .b(inputA32), .out(output32), .cin(1'b0), .cout(adder_1_cout));
  Comparator #(.width(32), .mode("unsigned")) comparator_1 (
    .a(inputB32), .b(inputA32), .gt(comparator_1_gt));  // open: eq, lt
  and and_1 (cout, adder_1_cout, control);
  and and_2 (sign_bit, comparator_1_gt, not_1_out);
endmodule
