// Logisim project compose_significand.circ as structural Verilog: 1 circuit, main circuit compose_significand
module compose_significand (
  input  [31:0] input_22_bits,
  output [31:0] composed_significand_26_bits_22_3_1
);


  assign composed_significand_26_bits_22_3_1 = {1'b1, input_22_bits[21:0], {9{1'b0}}};
endmodule
