// Logisim project exponent_difference.circ as structural Verilog: 1 circuit, main circuit exponent_difference_cal
module exponent_difference_cal (
  input  [31:0] greater_num,
  input  [31:0] smaller_num,
  output [8:0] exponent_diff_9bit
);

  Subtractor #(.width(9)) subtractor_1 (
    .a(greater_num[30:22]), .b(smaller_num[30:22]), .out(exponent_diff_9bit), .bin(1'b0));  // open: bout
endmodule
