// Logisim project exponent_minus_leftshift.circ as structural Verilog: 1 circuit, main circuit exponent_minus_leftshift
module exponent_minus_leftshift (
  input  [8:0] input9bit,
  input  [4:0] input5bit,
  output [8:0] \output ,
  output Underflow
);

  Subtractor #(.width(9)) subtractor_1 (
    .a(input9bit), .b({4'b0000, input5bit}), .out(\output ), .bin(1'b0));  // open: bout
  Comparator #(.width(10)) comparator_1 (
    .a({{5{1'b0}}, input5bit}), .b({1'b0, input9bit}), .gt(Underflow));  // open: eq, lt
endmodule
