// Logisim project extract_exponent.circ as structural Verilog: 1 circuit, main circuit extract_exponent
module extract_exponent (
  input  [31:0] num,
  output [8:0] exponent,
  output INF
);

  Comparator #(.width(10)) comparator_1 (.a({1'b0, num[30:22]}), .b(10'h1ff), .eq(INF));  // open: gt, lt

  assign exponent = num[30:22];
endmodule
