// Logisim project extract_sign_bit.circ as structural Verilog: 1 circuit, main circuit extract_sign_bit
module extract_sign_bit (
  input  [31:0] in_1,
  output sign_bit
);


  assign sign_bit = in_1[31];
endmodule
