// Logisim project final_one.circ as structural Verilog: 1 circuit, main circuit merge
module merge (
  input  sign,
  input  [8:0] exponent,
  input  [31:0] fraction,
  output Denormal,
  output [31:0] Output
);

  wire comparator_1_eq, comparator_2_eq;

  Comparator #(.width(10)) comparator_1 (.a({1'b0, exponent}), .b({10{1'b0}}), .eq(comparator_1_eq));  // open: gt, lt
  Comparator #(.width(23)) comparator_2 (
    .a({fraction[30:9], 1'b0}), .b({23{1'b0}}), .eq(comparator_2_eq));  // open: gt, lt
  Multiplexer #(.width(32), .enable("false")) multiplexer_1 (
    .in0({32{1'b0}}), .in1({sign, exponent, fraction[30:9]}), .out(Output), .sel(fraction[31]));
  and and_1 (Denormal, comparator_1_eq, comparator_2_eq, fraction[31]);
endmodule
