// Logisim project first_occuring one pos.circ as structural Verilog: 1 circuit, main circuit first_occuring_one pos
module first_occuring_one_pos (
  input  [31:0] num,
  output [4:0] first_occuring_Pos
);

  wire not_1_out, or_1_out;
  wire [4:0] multiplexer_1_out, priority_encoder_1_out, subtractor_1_out;

  Priority_Encoder #(.select(5)) priority_encoder_1 (
    .in0(num[0]), .in1(num[1]), .in2(num[2]), .in3(num[3]), .in4(num[4]), .in5(num[5]), .in6(num[6]),
    .in7(num[7]), .in8(num[8]), .in9(num[9]), .in10(num[10]), .in11(num[11]), .in12(num[12]), .in13(num[13]),
    .in14(num[14]), .in15(num[15]), .in16(num[16]), .in17(num[17]), .in18(num[18]), .in19(num[19]),
    .in20(num[20]), .in21(num[21]), .in22(num[22]), .in23(num[23]), .in24(num[24]), .in25(num[25]),
    .in26(num[26]), .in27(num[27]), .in28(num[28]), .in29(num[29]), .in30(num[30]), .in31(num[31]),
    .out(priority_encoder_1_out));  // open: gs, en_out, en_in
  or or_1 (or_1_out, num[0], num[1], num[2], num[3], num[4], num[5], num[6], num[7], num[8], num[9], num[10], num[11], num[12], num[13], num[14], num[15], num[17], num[18], num[19], num[20], num[21], num[22], num[23], num[24], num[25], num[26], num[27], num[28], num[29], num[30], num[31]);
  not not_1 (not_1_out, or_1_out);
  Multiplexer #(.width(5), .enable("false")) multiplexer_1 (
    .in0(priority_encoder_1_out), .in1({5{1'b0}}), .out(multiplexer_1_out), .sel(not_1_out));
  Subtractor #(.width(5)) subtractor_1 (
    .a({5{1'b1}}), .b(multiplexer_1_out), .out(subtractor_1_out), .bin(1'b0));  // open: bout
  Multiplexer #(.width(5), .enable("false")) multiplexer_2 (
    .in0(subtractor_1_out), .in1({5{1'b0}}), .out(first_occuring_Pos), .sel(not_1_out));
endmodule
