// Logisim project flags.circ as structural Verilog: 1 circuit, main circuit of_uf checker
module of_uf_checker (
  input  [8:0] in_1,
  output INF
);

  Comparator #(.width(9)) comparator_1 (.a(in_1), .b({9{1'b1}}), .eq(INF));  // open: gt, lt
endmodule
