// Logisim project fpa_main.circ as structural Verilog: 1 circuit, main circuit FPA
module FPA (
  input  [31:0] Input_1,
  input  [31:0] INput_2,
  output Zero_flag,
  output nan,
  output [31:0] out_5,
  output Ultimate_sign_bit,
  output INF,
  output Denormal_Num,
  output nan_2,
  output inf_2,
  output Denormal_Num_2,
  output nan_3,
  output Denormal_Num_3,
  output INF_3,
  output Underflow,
  output Overflow
);

  wire adder_sub_1_cout, adder_sub_1_sign_bit, and_1_out, extract_sign_bit_1_sign_bit,
       extract_sign_bit_2_sign_bit, invalid_num_checker_3_inf, invalid_num_checker_3_invalid_num,
       main_3_sign_bit, merge_1_denormal, n1_exponent_1_overflow, n1_exponent_2_overflow, not_1_out,
       or_3_out, rounded_1_cout, roundingfn_1_roundup, xnor_1_out;
  wire [1:0] main_1_zero_checker_bit;
  wire [4:0] first_occuring_one_pos_1_first_occuring_pos, multiplexer_2_out;
  wire [8:0] exponent_difference_cal_1_exponent_diff_9bit, exponent_minus_leftshift_1_output,
       extract_exponent_1_exponent, n1_exponent_1_exponent_controlbit, n1_exponent_2_exponent_controlbit;
  wire [31:0] absolute_val_significand_1_output32, adder_sub_1_output32,
       compose_significand_1_composed_significand_26_bits_22_3_1,
       compose_significand_2_composed_significand_26_bits_22_3_1, merge_1_output,
       rearrange_into_greater_smaller_1_greater_num, rearrange_into_greater_smaller_1_smaller_num,
       right_shift_frac_by_expon_diff_1_significand_shifted, right_shifted_expoent_1_output,
       right_shifted_expoent_2_output, rounded_1_rounded_out32, shifter_1_out;

  invalid_num_checker invalid_num_checker_1 (.\input (Input_1), .Invalid_Num(Denormal_Num_2), .inf(inf_2), .NAN(nan_2));
  invalid_num_checker invalid_num_checker_2 (.\input (INput_2), .Invalid_Num(Denormal_Num_3), .inf(INF_3), .NAN(nan_3));
  zero_checker_main main_1 (.in_1(Input_1), .zero_checker_bit(main_1_zero_checker_bit[0]));
  zero_checker_main main_2 (.in_1(INput_2), .zero_checker_bit(main_1_zero_checker_bit[1]));
  rearrange_into_greater_smaller rearrange_into_greater_smaller_1 (
    .in_1(Input_1), .in_2(INput_2), .Greater_NUM(rearrange_into_greater_smaller_1_greater_num),
    .Smaller_Num(rearrange_into_greater_smaller_1_smaller_num));
  extract_sign_bit extract_sign_bit_1 (
    .in_1(rearrange_into_greater_smaller_1_greater_num), .sign_bit(extract_sign_bit_1_sign_bit));
  extract_sign_bit extract_sign_bit_2 (
    .in_1(rearrange_into_greater_smaller_1_smaller_num), .sign_bit(extract_sign_bit_2_sign_bit));
  compose_significand compose_significand_1 (
    .input_22_bits(rearrange_into_greater_smaller_1_greater_num),
    .composed_significand_26_bits_22_3_1(compose_significand_1_composed_significand_26_bits_22_3_1));
  compose_significand compose_significand_2 (
    .input_22_bits(rearrange_into_greater_smaller_1_smaller_num),
    .composed_significand_26_bits_22_3_1(compose_significand_2_composed_significand_26_bits_22_3_1));
  exponent_difference_cal exponent_difference_cal_1 (
    .greater_num(rearrange_into_greater_smaller_1_greater_num),
    .smaller_num(rearrange_into_greater_smaller_1_smaller_num),
    .exponent_diff_9bit(exponent_difference_cal_1_exponent_diff_9bit));
  extract_exponent extract_exponent_1 (
    .num(rearrange_into_greater_smaller_1_greater_num), .exponent(extract_exponent_1_exponent));  // open: INF
  xnor xnor_1 (xnor_1_out, extract_sign_bit_1_sign_bit, extract_sign_bit_2_sign_bit);
  right_shift_frac_by_expon_diff right_shift_frac_by_expon_diff_1 (
    .expon_diff(exponent_difference_cal_1_exponent_diff_9bit),
    .significand(compose_significand_2_composed_significand_26_bits_22_3_1),
    .significand_shifted(right_shift_frac_by_expon_diff_1_significand_shifted));
  Multiplexer #(.enable("false")) multiplexer_1 (
    .in0(main_3_sign_bit), .in1(extract_sign_bit_2_sign_bit), .out(Ultimate_sign_bit), .sel(xnor_1_out));
  adder_sub adder_sub_1 (
    .inputB32(right_shift_frac_by_expon_diff_1_significand_shifted), .control(xnor_1_out),
    .inputA32(compose_significand_1_composed_significand_26_bits_22_3_1), .sign_bit(adder_sub_1_sign_bit),
    .output32(adder_sub_1_output32), .cout(adder_sub_1_cout));
  _1_exponent u_1_exponent_1 (
    .exponent(extract_exponent_1_exponent), .control_bit(and_1_out),
    .exponent_controlbit(n1_exponent_1_exponent_controlbit), .overflow(n1_exponent_1_overflow));  // open: INF
  and and_1 (and_1_out, xnor_1_out, adder_sub_1_cout);
  absolute_val_significand absolute_val_significand_1 (
    .input32(adder_sub_1_output32), .SignbitIn(adder_sub_1_sign_bit),
    .output32(absolute_val_significand_1_output32));
  sign_checker_main main_3 (.in_1(Input_1), .in_2(INput_2), .sign_bit(main_3_sign_bit));
  right_shifted_expoent right_shifted_expoent_1 (
    .input32(absolute_val_significand_1_output32), .controll(and_1_out),
    .\output (right_shifted_expoent_1_output));
  exponent_minus_leftshift exponent_minus_leftshift_1 (
    .input9bit(n1_exponent_1_exponent_controlbit), .input5bit(multiplexer_2_out),
    .\output (exponent_minus_leftshift_1_output), .Underflow(Underflow));
  first_occuring_one_pos first_occuring_one_pos_1 (
    .num(absolute_val_significand_1_output32),
    .first_occuring_Pos(first_occuring_one_pos_1_first_occuring_pos));
  _1_exponent u_1_exponent_2 (
    .exponent(exponent_minus_leftshift_1_output), .control_bit(rounded_1_cout),
    .exponent_controlbit(n1_exponent_2_exponent_controlbit), .overflow(n1_exponent_2_overflow));  // open: INF
  Multiplexer #(.width(5), .enable("false")) multiplexer_2 (
    .in0(first_occuring_one_pos_1_first_occuring_pos), .in1({5{1'b0}}), .out(multiplexer_2_out),
    .sel(and_1_out));
  Shifter #(.width(32)) shifter_1 (
    .in(right_shifted_expoent_1_output), .\dist (multiplexer_2_out), .out(shifter_1_out));
  zero_checker_main main_4 (.in_1(out_5), .zero_checker_bit(Zero_flag));
  roundingFn roundingfn_1 (.input32(shifter_1_out), .roundup(roundingfn_1_roundup));
  rounded rounded_1 (
    .input_32(shifter_1_out), .rounding_control(roundingfn_1_roundup),
    .rounded_out32(rounded_1_rounded_out32), .cout(rounded_1_cout));
  or or_1 (Overflow, n1_exponent_2_overflow, n1_exponent_1_overflow);
  merge merge_1 (
    .sign(Ultimate_sign_bit), .exponent(n1_exponent_2_exponent_controlbit),
    .fraction(right_shifted_expoent_2_output), .Denormal(merge_1_denormal), .Output(merge_1_output));
  right_shifted_expoent right_shifted_expoent_2 (
    .input32(rounded_1_rounded_out32), .controll(rounded_1_cout), .\output (right_shifted_expoent_2_output));
  Multiplexer #(.select(2), .width(32), .enable("false")) multiplexer_3 (
    .in0(merge_1_output), .in1(INput_2), .in2(Input_1), .in3({32{1'b0}}), .out(out_5),
    .sel(main_1_zero_checker_bit));
  invalid_num_checker invalid_num_checker_3 (
    .\input (out_5), .Invalid_Num(invalid_num_checker_3_invalid_num), .inf(invalid_num_checker_3_inf),
    .NAN(nan));
  or or_2 (Denormal_Num, invalid_num_checker_3_invalid_num, merge_1_denormal);
  not not_1 (not_1_out, or_3_out);
  or or_3 (or_3_out, Underflow, Overflow);
  and and_2 (INF, not_1_out, invalid_num_checker_3_inf);

  // Notes on the sheet:
  //   sign1
  //   sign2
  //   Appending bit
  //   absolute val
endmodule
