// Logisim project invalid_num_checker.circ as structural Verilog: 1 circuit, main circuit invalid_num_checker
module invalid_num_checker (
  input  [31:0] \input ,
  output Invalid_Num,
  output inf,
  output NAN
);

  wire and_1_out, not_1_out, not_2_out, or_1_out, or_2_out;

  or or_1 (or_1_out, \input [22], \input [23], \input [24], \input [25], \input [26], \input [27], \input [28], \input [29], \input [30]);
  and and_1 (and_1_out, \input [24], \input [30], \input [22], \input [23], \input [25], \input [26], \input [27], \input [28], \input [29]);
  or or_2 (or_2_out, \input [0], \input [1], \input [2], \input [3], \input [4], \input [5], \input [6], \input [7], \input [8], \input [9], \input [10], \input [11], \input [12], \input [13], \input [14], \input [15], \input [16], \input [17], \input [18], \input [19], \input [20], \input [21]);
  not not_1 (not_1_out, or_1_out);
  not not_2 (not_2_out, or_2_out);
  and and_2 (Invalid_Num, or_2_out, not_1_out);
  and and_3 (NAN, or_2_out, and_1_out);
  and and_4 (inf, not_2_out, and_1_out);
endmodule
