// Logisim project rearrange.circ as structural Verilog: 1 circuit, main circuit rearrange_into_greater_smaller
module rearrange_into_greater_smaller (
  input  [31:0] in_1,
  input  [31:0] in_2,
  output [31:0] Greater_NUM,
  output [31:0] Smaller_Num
);

  wire comparator_1_gt, not_1_out;

  Comparator #(.width(10)) comparator_1 (
    .a({1'b0, in_1[30:22]}), .b({1'b0, in_2[30:22]}), .gt(comparator_1_gt));  // open: eq, lt
  not not_1 (not_1_out, comparator_1_gt);
  Multiplexer #(.width(32), .enable("false")) multiplexer_1 (
    .in0(in_2), .in1(in_1), .out(Greater_NUM), .sel(comparator_1_gt));
  Multiplexer #(.width(32), .enable("false")) multiplexer_2 (
    .in0(in_2), .in1(in_1), .out(Smaller_Num), .sel(not_1_out));
endmodule
