// Logisim project right_shifted_expnent.circ as structural Verilog: 1 circuit, main circuit right_shifted_expoent
module right_shifted_expoent (
  input  [31:0] input32,
  input  controll,
  output [31:0] \output 
);

  wire [31:0] shifter_1_out;

  Shifter #(.width(32), .shift("lr")) shifter_1 (.in(input32), .\dist ({4'b0000, controll}), .out(shifter_1_out));
  Adder #(.width(32)) adder_1 (
    .a(shifter_1_out), .b({controll, {31{1'b0}}}), .out(\output ), .cin(1'b0));  // open: cout
endmodule
