// Logisim project rightshift_fraction_by_expon_diff.circ as structural Verilog: 1 circuit, main circuit right_shift_frac_by_expon_diff
module right_shift_frac_by_expon_diff (
  input  [8:0] expon_diff,
  input  [31:0] significand,
  output [31:0] significand_shifted
);

  wire comparator_1_gt;
  wire [31:0] shifter_1_out;

  Shifter #(.width(32), .shift("lr")) shifter_1 (.in(significand), .\dist (expon_diff[4:0]), .out(shifter_1_out));
  Comparator #(.width(10)) comparator_1 (.a({1'b0, expon_diff}), .b(10'h16), .gt(comparator_1_gt));  // open: eq, lt
  Multiplexer #(.width(32), .enable("false")) multiplexer_1 (
    .in0(shifter_1_out), .in1({32{1'b0}}), .out(significand_shifted), .sel(comparator_1_gt));
endmodule
