// Logisim project round_up_func.circ as structural Verilog: 1 circuit, main circuit roundingFn
module roundingFn (
  input  [31:0] input32,
  output roundup
);

  wire or_1_out;

  or or_1 (or_1_out, input32[9], input32[7], input32[6]);
  and and_1 (roundup, input32[8], or_1_out);
endmodule
