// Logisim project rounded.circ as structural Verilog: 1 circuit, main circuit rounded
module rounded (
  input  [31:0] input_32,
  input  rounding_control,
  output [31:0] rounded_out32,
  output cout
);

  Adder #(.width(32)) adder_1 (
    .a(input_32), .b({{22{1'b0}}, rounding_control, {9{1'b0}}}), .out(rounded_out32), .cin(1'b0), .cout(cout));
endmodule
