// Logisim project sign_checker.circ as structural Verilog: 1 circuit, main circuit main
module main (
  input  [31:0] in_1,
  input  [31:0] in_2,
  output sign_bit
);

  wire not_1_out;
  wire [30:0] multiplexer_1_out, multiplexer_2_out;

  Multiplexer #(.width(31), .enable("false")) multiplexer_1 (
    .in0(in_1[30:0]), .in1(in_2[30:0]), .out(multiplexer_1_out), .sel(in_1[31]));
  not not_1 (not_1_out, in_1[31]);
  Multiplexer #(.width(31), .enable("false")) multiplexer_2 (
    .in0(in_1[30:0]), .in1(in_2[30:0]), .out(multiplexer_2_out), .sel(not_1_out));
  Comparator #(.width(31), .mode("unsigned")) comparator_1 (
    .a(multiplexer_1_out), .b(multiplexer_2_out), .lt(sign_bit));  // open: gt, eq
endmodule
