// Logisim project zero_checker.circ as structural Verilog: 1 circuit, main circuit main
module main (
  input  [31:0] in_1,
  output zero_checker_bit
);

  wire or_1_out;

  or or_1 (or_1_out, in_1[0], in_1[1], in_1[2], in_1[3], in_1[4], in_1[5], in_1[6], in_1[7], in_1[8], in_1[9], in_1[10], in_1[11], in_1[12], in_1[13], in_1[14], in_1[15], in_1[16], in_1[17], in_1[18], in_1[19], in_1[20], in_1[21], in_1[22], in_1[23], in_1[24], in_1[25], in_1[26], in_1[27], in_1[28], in_1[29], in_1[30]);
  not not_1 (zero_checker_bit, or_1_out);
endmodule
